// Logisim project CPU2.circ as structural Verilog: 1 circuit, main circuit main
module main (
);

  wire big_rom_1_p1, CLK, HALT, PROG_NEXT, PROG_REG_WRITE, pull_resistor_1_node, pull_resistor_2_node,
       SAVE_IR;
  wire [2:0] PROG_REG_ADDR;
  wire [7:0] counter_2_q, IR_q, pull_resistor_3_node;
  wire [15:0] counter_1_q;
  wire [23:0] IR_q_2;
  wire [31:0] PROG_data;

  Clock clock_1 (.out(CLK));
  ROM #(.addrWidth(16), .dataWidth(32)) PROG (.addr(counter_1_q), .data(PROG_data));
  Counter #(.width(16), .max('hffff)) counter_1 (
    .up(pull_resistor_1_node), .count(PROG_NEXT), .clk(CLK), .Q(counter_1_q));  // open: clr, load, D, carry
  Pull_Resistor #(.pull(1)) pull_resistor_1 (.node(pull_resistor_1_node));
  Counter counter_2 (
    .load(SAVE_IR), .up(pull_resistor_2_node), .count(pull_resistor_2_node), .clk(CLK),
    .D(pull_resistor_3_node), .Q(counter_2_q));  // open: clr, carry
  Pull_Resistor #(.pull(1)) pull_resistor_2 (.node(pull_resistor_2_node));
  Pull_Resistor pull_resistor_3 (.node(pull_resistor_3_node));
  Register #(.width(32)) IR (.D(PROG_data), .en(SAVE_IR), .clk(CLK), .Q({IR_q, IR_q_2}));  // open: clr
  // Big_ROM #(.addressWidth(40)) big_rom_1: pin names not known; wires that end beside it: big_rom_1_p1, IR_q
  // Splitter #(.fanout(32), .incoming(32), .appear("right"), .spacing("double")) splitter_1: pin names not known; wires that end beside it: big_rom_1_p1, HALT, SAVE_IR
  // Splitter #(.fanout(3), .incoming(3), .appear("center"), .spacing("double")) splitter_2: pin names not known; wires that end beside it: PROG_NEXT, PROG_REG_WRITE, PROG_REG_ADDR
  // Register_Bank #(.width(32), .registerCount(8), .portCount(1)) register_bank_1: pin names not known; wires that end beside it: PROG_REG_ADDR, CLK, PROG_REG_WRITE, PROG_data

  // Notes on the sheet:
  //   contents of PROG (hex, n*v repeats v):
  //   80 1 81 2 82 3 83 4 80 10 81 20 82 30 83 40
endmodule
